# Fritzing sketch Schaltung (TMC2209)_v2 (saved by Fritzing 0.9.10b)

parts:
  Bauteil2 = GY-VL53L0XV2 Laser Ranger Module
  Bauteil3 = GY-VL53L0XV2 Laser Ranger Module
  S3 = D2F-FL Omron Snap Action Limit Switch with Level
  S4 = D2F-FL Omron Snap Action Limit Switch with Level
  SCW05B-3 = SCW05B-05
  U5 = ESP32-38PinWide [part_number=ESP32-38PinWide]
  C2 = Electrolytic Capacitor [capacitance=100µF voltage=16V package="0807 [SMD, electrolytic]"]
  D4 = Schottky Diode [part_number=1N5819 package="Melf DO-213 AB [SMD]"]
  D5 = Schottky Diode [part_number=1N5819 package="Melf DO-213 AB [SMD]"]
  R15 = Resistor [tolerance=±5% power=0.25 resistance=100 package=THT]
  M1 = Stepper Motor - Bipolar
  Mod1 = TMC2209 [package=THT]
  S5 = Pushbutton [package="[SMD]"]
  S6 = Pushbutton [package="[SMD]"]
  R16 = Resistor [tolerance=±5% power=0.25 resistance=12k package=THT]
  R18 = Resistor [tolerance=±5% power=0.25 resistance=12k package=THT]  # not connected
  R19 = Resistor [tolerance=±5% power=0.25 resistance=12k package=THT]
  Bauteil4 = Arduino Uno (Rev3)

nets:
  VCC: Bauteil2.VCC, Bauteil3.VCC, U5.3.3
  GND: Bauteil2.GND, Bauteil3.GND, SCW05B-3.GND, U5.GND, Bauteil4.GND
  N1: Bauteil2.SCL, Bauteil3.SCL, U5.GPIO22
  N2: Bauteil2.SDA, Bauteil3.SDA, U5.GPIO21
  N3: Bauteil2.XSHUT, U5.GPIO19
  N4: Bauteil3.XSHUT, U5.GPIO23
  N5: S3.Pin_1, S4.Pin_3
  N6: S3.Pin_3, Mod1.VM
  N7: U5.GPIO35, Bauteil4.D9_PWM
  N8: U5.GPIO25, Mod1.EN
  N9: U5.GPIO26, Mod1.Step
  N10: U5.GPIO27, Mod1.Dir
  N11: U5.VIN, D4.cathode
  N12: C2.+, D5.anode, R15.Pin_1
  N13: M1.A, Mod1.A2
  N14: M1.C, Mod1.B1
  N15: M1.B, Mod1.A1
  N16: M1.D, Mod1.B2
  N17: Mod1.GND, Mod1.MS2
  N18: Mod1.VDD, Mod1.MS1
  N19: S5.Pin_3, S5.Pin_4, R16.Pin_0
  N20: S6.Pin_1, S6.Pin_2, R19.Pin_0

notes:
  DC-DC Wandler
  GND
  5V
  12V
  IN
  DC+
  DC-
  30mA
  200mA
  Schottky-Diode 1N5819
  100
  16V 100µF
  NC
  C
  Rollentaster (Endschalter)
  Treiber für Schrittmotor (TMC2209)
  Schrittmotor (12V, 2A)
  Laser Distanzsensor (je 40 mA)
  nach links
  nach rechts
  12K
  Taster zum manuellen
  verfahren der Rollenzentrierung
  Arduino von der SchneideMaschine

custom parts:
  GY-VL53L0XV2 Laser Ranger Module: The GY-VL53L0XV2 is based on the VL53L0X from ST Microelectronics, a time-of-flight ranging system integrated into a compact module.
  D2F-FL Omron Snap Action Limit Switch with Level: Snap action switch with stainless steel lever.
  ESP32-38PinWide: Generic 38-Pin ESP32 with wide format (only access to one side of pins on a breadboard) based on Stephen Lilley's HiLetgo ESP-WROOM-32 ESP32 ESP-32S Development Board.
  TMC2209: TMC2209-LA stepper motor controller and driver. Supply voltage 4.75-28V Iphase up to 1.77A rms (2.5A peak)
