# Fritzing sketch Schaltung_v2 (saved by Fritzing 0.9.10b)

parts:
  Bauteil2 = GY-VL53L0XV2 Laser Ranger Module
  Bauteil3 = GY-VL53L0XV2 Laser Ranger Module
  L298N1 = L298N DC motor driver
  S3 = D2F-FL Omron Snap Action Limit Switch with Level
  S4 = D2F-FL Omron Snap Action Limit Switch with Level
  U5 = ESP32-38PinWide [part_number=ESP32-38PinWide]
  C2 = Electrolytic Capacitor [capacitance=100µF voltage=16V package="0807 [SMD, electrolytic]"]
  D4 = Schottky Diode [part_number=1N5819 package="Melf DO-213 AB [SMD]"]
  D5 = Schottky Diode [part_number=1N5819 package="Melf DO-213 AB [SMD]"]
  R15 = Resistor [tolerance=±5% power=0.25 resistance=100 package=THT]
  M1 = Stepper Motor - Bipolar

nets:
  VCC: Bauteil2.VCC, Bauteil3.VCC, U5.3.3
  GND: Bauteil2.GND, Bauteil3.GND, U5.GND, C2.+
  N1: Bauteil2.SCL, Bauteil3.SCL, U5.GPIO22
  N2: Bauteil2.SDA, Bauteil3.SDA, U5.GPIO21
  N3: Bauteil2.XSHUT, U5.GPIO19
  N4: Bauteil3.XSHUT, U5.GPIO23
  N5: L298N1.OUT1, M1.A
  N6: L298N1.OUT2, M1.B
  N7: L298N1.OUT3, M1.D
  N8: L298N1.OUT4, M1.C
  N9: L298N1.12V, S3.Pin_3
  N10: L298N1.5V#7, D4.anode
  N11: L298N1.5V#9, L298N1.ENA
  N12: L298N1.5V#10, L298N1.ENB
  N13: L298N1.IN1, U5.GPIO13
  N14: L298N1.IN2, U5.GPIO12
  N15: L298N1.IN3, U5.GPIO14
  N16: L298N1.IN4, U5.GPIO27
  N17: S3.Pin_1, S4.Pin_3
  N18: U5.VIN, D4.cathode
  N19: C2.-, D5.anode, R15.Pin_1

notes:
  GND
  5V out
  12V in
  IN
  DC+
  DC-
  200mA
  Schottky-Diode 1N5819
  100
  16V 100µF
  NC
  C
  Rollentaster (Endschalter)
  Treiber für Schrittmotor
  Schrittmotor (12V, 2A)
  Laser Distanzsensor (je 40 mA)
  12V
  - Wenn der Jumper "5VEN" gesetzt ist, dann kann man den 5V anschluss als Strom-Quelle nutzen

custom parts:
  GY-VL53L0XV2 Laser Ranger Module: The GY-VL53L0XV2 is based on the VL53L0X from ST Microelectronics, a time-of-flight ranging system integrated into a compact module.
  L298N DC motor driver: 2x DC motor driver with 78M05 positive voltage regulator (7..35 V) L298N: max 46 V, 2 A Set 5 V Enable jumper to enable 5 V regultor (needed for the L298N) and +5 V output at screw terminal or supply external +5 V at screw terminal Set ENA and/or ENB to +5 V to enable motor permanently or supply ENA and/or ENB with PWM signal IN1 and IN2 set rotation directory for motor A (OUT1/OUT2) IN2 and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
  D2F-FL Omron Snap Action Limit Switch with Level: Snap action switch with stainless steel lever.
  ESP32-38PinWide: Generic 38-Pin ESP32 with wide format (only access to one side of pins on a breadboard) based on Stephen Lilley's HiLetgo ESP-WROOM-32 ESP32 ESP-32S Development Board.
