# Fritzing sketch TMC2209 - Example (saved by Fritzing 0.9.10b)

parts:
  U5 = ESP32-38PinWide [part_number=ESP32-38PinWide]
  M1 = Stepper Motor - Bipolar
  Mod1 = TMC2209 [package=THT]

nets:
  N1: U5.GPIO25, Mod1.EN
  N2: U5.GPIO26, Mod1.Step
  N3: U5.GPIO27, Mod1.Dir
  N4: M1.A, Mod1.A2
  N5: M1.C, Mod1.B1
  N6: M1.B, Mod1.A1
  N7: M1.D, Mod1.B2
  N8: Mod1.GND, Mod1.MS2
  N9: Mod1.VDD, Mod1.MS1

notes:
  GND
  12V
  IN
  DC+
  DC-
  Treiber für Schrittmotor (TMC 2209)
  Schrittmotor (12V, 2A)
  2 Mikroschritte (MS1=VDD, MS2=GND)
  Die Pins MS1 und MS2 bestimmen die Feinheit der Microschritte

custom parts:
  ESP32-38PinWide: Generic 38-Pin ESP32 with wide format (only access to one side of pins on a breadboard) based on Stephen Lilley's HiLetgo ESP-WROOM-32 ESP32 ESP-32S Development Board.
  TMC2209: TMC2209-LA stepper motor controller and driver. Supply voltage 4.75-28V Iphase up to 1.77A rms (2.5A peak)
